// Logisim project FullBoard.circ as structural Verilog: 1 circuit, main circuit main
module main (
  input  a0,
  input  a1,
  input  a2,
  input  a3,
  input  a4,
  input  a5,
  input  a6,
  input  a7,
  input  a8,
  output Exit
);

  and and_1 (Exit, a0, a1, a2, a3, a4, a5, a6, a7, a8);
endmodule
