// Logisim project TTT_Epsilon.circ as structural Verilog: 1 circuit, main circuit main
module main (
  input  [3:0] in_1,
  input  [3:0] CPU_Input_Logic,
  input  in_3
);

  wire and_1_out, and_2_out, and_3_out, and_4_out, Cpuwin, d_ff_1_qn, dmx0, dmx1, dmx2, dmx3, dmx4, dmx5,
       dmx6, dmx7, dmx8, full, main_9_start, or_1_out, or_2_out, or_3_out, or_4_out, or_5_out, or_6_out,
       or_7_out, or_8_out, or_9_out, special, t_ff_1_q, t_ff_2_q, ts0, ts1, ts2, ts3, ts4, ts5, ts6, ts7,
       ts8, undriven, undriven_2, used0, used1, used2, used3, used4, used5, used6, used7, used8, Userwin,
       who, win;
  wire [3:0] cpuout, to0, to1, to2, to3, to4, to5, to6, to7, to8, userout;

  Hex_Digit_Display hex_digit_display_1 (.value(to0));  // open: dp
  Hex_Digit_Display hex_digit_display_2 (.value(to3));  // open: dp
  Hex_Digit_Display hex_digit_display_3 (.value(to6));  // open: dp
  UserControl_main main_1 (.userin(in_1), .trigu(in_3), .userout(userout));
  // Probe on undriven
  Hex_Digit_Display hex_digit_display_4 (.value(to1));  // open: dp
  Hex_Digit_Display hex_digit_display_5 (.value(to4));  // open: dp
  Hex_Digit_Display hex_digit_display_6 (.value(to7));  // open: dp
  // Probe on undriven
  or or_1 (or_1_out, win, full);
  or or_2 (or_2_out, win, full);
  or or_3 (or_3_out, win, full);
  Used_main main_2 (
    .trigu(in_3), .dmx0(dmx0), .win_full(or_1_out), .who(who), .truesingle(ts0), .used(used0),
    .trueoutput(to0));
  Used_main main_3 (
    .trigu(in_3), .dmx0(dmx3), .win_full(or_2_out), .who(who), .truesingle(ts3), .used(used3),
    .trueoutput(to3));
  Used_main main_4 (
    .trigu(in_3), .dmx0(dmx6), .win_full(or_3_out), .who(who), .truesingle(ts6), .used(used6),
    .trueoutput(to6));
  // Probe on undriven_2
  Hex_Digit_Display hex_digit_display_7 (.value(to2));  // open: dp
  Hex_Digit_Display hex_digit_display_8 (.value(to5));  // open: dp
  Hex_Digit_Display hex_digit_display_9 (.value(to8));  // open: dp
  // Probe on undriven_2
  UserControl_main main_5 (.userin(CPU_Input_Logic), .trigu(in_3), .userout(cpuout));
  or or_4 (or_4_out, win, full);
  or or_5 (or_5_out, win, full);
  or or_6 (or_6_out, win, full);
  LED led_1 (.in(t_ff_1_q));
  Used_main main_6 (
    .trigu(in_3), .dmx0(dmx1), .win_full(or_4_out), .who(who), .truesingle(ts1), .used(used1),
    .trueoutput(to1));
  Used_main main_7 (
    .trigu(in_3), .dmx0(dmx4), .win_full(or_5_out), .who(who), .truesingle(ts4), .used(used4),
    .trueoutput(to4));
  Used_main main_8 (
    .trigu(in_3), .dmx0(dmx7), .win_full(or_6_out), .who(who), .truesingle(ts7), .used(used7),
    .trueoutput(to7));
  and and_1 (and_1_out, in_3, ~special);  // AND_Gate
  LED led_2 (.in(and_2_out));
  and and_2 (and_2_out, ~t_ff_1_q, ~t_ff_2_q);  // AND_Gate
  T_Flip_Flop t_ff_1 (.clk(Userwin), .Q(t_ff_1_q), .reset(and_3_out));  // open: T, Qn, preset, en
  and and_3 (and_3_out, Userwin, win);
  D_Flip_Flop #(.trigger("falling")) d_ff_1 (
    .clk(and_1_out), .D(d_ff_1_qn), .Q(who), .Qn(d_ff_1_qn), .preset(main_9_start));  // open: en, reset
  or or_7 (or_7_out, win, full);
  or or_8 (or_8_out, win, full);
  or or_9 (or_9_out, win, full);
  Start_main main_9 (
    .used0(used0), .used1(used1), .used2(used2), .used3(used3), .used4(used4), .used5(used5), .used6(used6),
    .used7(used7), .used8(used8), .start(main_9_start));
  LED led_3 (.in(t_ff_2_q));
  T_Flip_Flop t_ff_2 (.clk(Cpuwin), .Q(t_ff_2_q), .reset(and_4_out));  // open: T, Qn, preset, en
  and and_4 (and_4_out, Cpuwin, win);
  Used_main main_10 (
    .trigu(in_3), .dmx0(dmx2), .win_full(or_7_out), .who(who), .truesingle(ts2), .used(used2),
    .trueoutput(to2));
  Used_main main_11 (
    .trigu(in_3), .dmx0(dmx5), .win_full(or_8_out), .who(who), .truesingle(ts5), .used(used5),
    .trueoutput(to5));
  Used_main main_12 (
    .trigu(in_3), .dmx0(dmx8), .win_full(or_9_out), .who(who), .truesingle(ts8), .used(used8),
    .trueoutput(to8));
  Choice_main main_13 (
    .cpuout(cpuout), .userout(userout), .who(who), .dmx0(dmx0), .dmx1(dmx1), .dmx2(dmx2), .dmx3(dmx3),
    .dmx4(dmx4), .dmx5(dmx5), .dmx6(dmx6), .dmx7(dmx7), .dmx8(dmx8), .special(special));
  WinCheck_main main_14 (
    .a0(ts0), .a1(ts1), .a2(ts2), .a3(ts3), .a4(ts4), .a5(ts5), .a6(ts6), .a7(ts7), .a8(ts8), .Exit(win),
    .UserWin(Userwin), .CPUwin(Cpuwin));
  FullBoard_main main_15 (
    .a0(used0), .a1(used1), .a2(used2), .a3(used3), .a4(used4), .a5(used5), .a6(used6), .a7(used7),
    .a8(used8), .Exit(full));

  // Other names for the same wires on the sheet: trigger = in_3

  // Notes on the sheet:
  //   send signal
  //   0001
  //   0100
  //   0111
  //   User Input Logic
  //   Tic-Tac-Toe
  //   Final Output
  //   0010
  //   0101
  //   1000
  //   Execute
  //   Push this to send choice to the board
  //   _________________________________________
  //   __________________________________________
  //   0011
  //   0110
  //   1001
  //   User Won 
  //   Memory Cells 
  //   Turn Logic
  //   1 for user, 0 for computer
  //   Nobody's won yet!
  //   Cpu Won
  //   ^ Whats the choice
  //   Check For Win/Full Board
endmodule
