// Logisim project TTT_Flamingo.circ as structural Verilog: 1 circuit, main circuit main
module main (
  input  [3:0] in_1,
  input  [3:0] CPU_Input_Logic,
  input  in_3,
  input  in_4
);

  wire and_1_out, and_2_out, and_3_out, and_4_out, and_5_out, and_6_out, and_7_out, and_8_out, and_9_out,
       and_10_out, and_11_out, Cpuwin, dmx0, dmx1, dmx2, dmx3, dmx4, dmx5, dmx6, dmx7, dmx8, full,
       main_9_start, not_1_out, or_1_out, or_2_out, or_3_out, or_4_out, or_5_out, or_6_out, or_7_out,
       or_9_out, or_10_out, or_11_out, or_12_out, rwin, special, t_ff_1_q, t_ff_2_q, tie, ts0, ts1, ts2, ts3,
       ts4, ts5, ts6, ts7, ts8, undriven, undriven_2, used0, used1, used2, used3, used4, used5, used6, used7,
       used8, Userwin, who, win;
  wire [3:0] cpuout, to0, to1, to2, to3, to4, to5, to6, to7, to8, userout;

  Hex_Digit_Display hex_digit_display_1 (.value(to0));  // open: dp
  Hex_Digit_Display hex_digit_display_2 (.value(to3));  // open: dp
  Hex_Digit_Display hex_digit_display_3 (.value(to6));  // open: dp
  or or_1 (or_1_out, rwin, full);
  or or_2 (or_2_out, rwin, full);
  or or_3 (or_3_out, rwin, full);
  UserControl_main main_1 (.userin(in_1), .trigu(in_3), .userout(userout));
  // Probe on undriven
  Hex_Digit_Display hex_digit_display_4 (.value(to1));  // open: dp
  Hex_Digit_Display hex_digit_display_5 (.value(to4));  // open: dp
  Hex_Digit_Display hex_digit_display_6 (.value(to7));  // open: dp
  // Probe on undriven
  and and_1 (and_1_out, or_1_out, ~special);  // AND_Gate
  and and_2 (and_2_out, or_2_out, ~special);  // AND_Gate
  and and_3 (and_3_out, or_3_out, ~special);  // AND_Gate
  // Used_main main_2: pin names not known; wires that end beside it: in_3, dmx0, and_1_out, who, ts0, in_4, used0, to0
  // Used_main main_3: pin names not known; wires that end beside it: in_3, dmx3, and_2_out, who, ts3, in_4, used3, to3
  // Used_main main_4: pin names not known; wires that end beside it: in_3, dmx6, and_3_out, who, ts6, in_4, used6, to6
  // Probe on undriven_2
  Hex_Digit_Display hex_digit_display_7 (.value(to2));  // open: dp
  Hex_Digit_Display hex_digit_display_8 (.value(to5));  // open: dp
  Hex_Digit_Display hex_digit_display_9 (.value(to8));  // open: dp
  // Probe on undriven_2
  UserControl_main main_5 (.userin(CPU_Input_Logic), .trigu(in_4), .userout(cpuout));
  or or_4 (or_4_out, rwin, full);
  or or_5 (or_5_out, rwin, full);
  or or_6 (or_6_out, rwin, full);
  and and_4 (and_4_out, or_4_out, ~special);  // AND_Gate
  and and_5 (and_5_out, or_5_out, ~special);  // AND_Gate
  and and_6 (and_6_out, or_6_out, ~special);  // AND_Gate
  LED led_1 (.in(t_ff_1_q));
  // Used_main main_6: pin names not known; wires that end beside it: in_3, dmx1, and_4_out, who, ts1, in_4, used1, to1
  // Used_main main_7: pin names not known; wires that end beside it: in_3, dmx4, and_5_out, who, ts4, in_4, used4, to4
  // Used_main main_8: pin names not known; wires that end beside it: in_3, dmx7, and_6_out, who, ts7, in_4, used7, to7
  LED led_2 (.in(and_7_out));
  and and_7 (and_7_out, ~t_ff_1_q, ~tie, ~t_ff_2_q);  // AND_Gate
  T_Flip_Flop t_ff_1 (.Q(t_ff_1_q), .preset(Userwin), .reset(or_7_out));  // open: clk, T, Qn, en
  or or_7 (or_7_out, Cpuwin, tie);
  D_Flip_Flop #(.trigger("falling")) d_ff_1 (
    .Q(who), .preset(not_1_out), .reset(main_9_start));  // open: clk, D, Qn, en
  not not_1 (not_1_out, main_9_start);
  or or_8 (rwin, t_ff_1_q, t_ff_2_q);
  or or_9 (or_9_out, rwin, full);
  TurnLogic_main main_9 (
    .used0(used0), .used1(used1), .used2(used2), .used3(used3), .used4(used4), .used5(used5), .used6(used6),
    .used7(used7), .used8(used8), .start(main_9_start));
  LED led_3 (.in(t_ff_2_q));
  T_Flip_Flop t_ff_2 (.Q(t_ff_2_q), .preset(Cpuwin), .reset(or_10_out));  // open: clk, T, Qn, en
  or or_10 (or_10_out, Userwin, tie);
  or or_11 (or_11_out, rwin, full);
  and and_8 (and_8_out, or_11_out, ~special);  // AND_Gate
  and and_9 (and_9_out, or_12_out, ~special);  // AND_Gate
  or or_12 (or_12_out, rwin, full);
  and and_10 (and_10_out, or_9_out, ~special);  // AND_Gate
  // Used_main main_10: pin names not known; wires that end beside it: in_3, dmx2, and_8_out, who, ts2, in_4, used2, to2
  // Used_main main_11: pin names not known; wires that end beside it: in_3, dmx5, and_9_out, who, ts5, in_4, used5, to5
  // Used_main main_12: pin names not known; wires that end beside it: in_3, dmx8, and_10_out, who, ts8, in_4, used8, to8
  LED led_4 (.in(tie));
  D_Flip_Flop d_ff_2 (.Q(tie), .preset(and_11_out));  // open: clk, D, Qn, en, reset
  and and_11 (and_11_out, full, ~rwin);  // AND_Gate
  Choice_main main_13 (
    .cpuout(cpuout), .userout(userout), .who(who), .dmx0(dmx0), .dmx1(dmx1), .dmx2(dmx2), .dmx3(dmx3),
    .dmx4(dmx4), .dmx5(dmx5), .dmx6(dmx6), .dmx7(dmx7), .dmx8(dmx8), .special(special));
  WinCheck_main main_14 (
    .a0(ts0), .a1(ts1), .a2(ts2), .a3(ts3), .a4(ts4), .a5(ts5), .a6(ts6), .a7(ts7), .a8(ts8), .Exit(win),
    .UserWin(Userwin), .CPUwin(Cpuwin));
  FullBoard_main main_15 (
    .a0(used0), .a1(used1), .a2(used2), .a3(used3), .a4(used4), .a5(used5), .a6(used6), .a7(used7),
    .a8(used8), .Exit(full));

  // Other names for the same wires on the sheet: cputrigger = in_4; trigger = in_3

  // Notes on the sheet:
  //   send signal
  //   0001
  //   0100
  //   0111
  //   User Input Logic
  //   Tic-Tac-Toe
  //   Final Output
  //   0010
  //   0101
  //   1000
  //   UserExecute
  //   Push this to send choice to the board
  //   CpuExecute
  //   Push this to send choice to the board
  //   _________________________________________
  //   __________________________________________
  //   0011
  //   0110
  //   1001
  //   User Won 
  //   Memory Cells 
  //   Turn Logic
  //   1 for user, 0 for computer
  //   Nobody's won yet!
  //   Cpu Won
  //   Tied!
  //   ^ Whats the choice
  //   Check For Win/Full Board
endmodule
